# Fritzing sketch pcb_schema (saved by Fritzing 0.9.10b)
breadboards: 2

parts:
  IN12A1 = IN12A [part_number=IN12A]
  MSPA42 = TRANSISTOR_NPN [package=to-92-ammo]
  MSPA43 = TRANSISTOR_NPN [package=to-92-ammo]
  MSPA44 = TRANSISTOR_NPN [package=to-92-ammo]
  MSPA45 = TRANSISTOR_NPN [package=to-92-ammo]
  MSPA46 = TRANSISTOR_NPN [package=to-92-ammo]
  MSPA47 = TRANSISTOR_NPN [package=to-92-ammo]
  MSPA48 = TRANSISTOR_NPN [package=to-92-ammo]
  MSPA49 = TRANSISTOR_NPN [package=to-92-ammo]
  MSPA50 = TRANSISTOR_NPN [package=to-92-ammo]
  MSPA51 = TRANSISTOR_NPN [package=to-92-ammo]
  MSPA52 = TRANSISTOR_NPN [package=to-92-ammo]
  R1 = Resistor [tolerance=±5% resistance=15k package="1206 [SMD]"]
  R2 = Resistor [tolerance=±5% resistance=15k package="1206 [SMD]"]
  R3 = Resistor [tolerance=±5% resistance=15k package="1206 [SMD]"]
  R4 = Resistor [tolerance=±5% resistance=15k package="1206 [SMD]"]
  R5 = Resistor [tolerance=±5% resistance=15k package="1206 [SMD]"]
  R6 = Resistor [tolerance=±5% resistance=15k package="1206 [SMD]"]
  R7 = Resistor [tolerance=±5% resistance=15k package="1206 [SMD]"]
  R8 = Resistor [tolerance=±5% resistance=15k package="1206 [SMD]"]
  R9 = Resistor [tolerance=±5% resistance=15k package="1206 [SMD]"]
  R10 = Resistor [tolerance=±5% resistance=15k package="1206 [SMD]"]
  R11 = Resistor [tolerance=±5% resistance=15k package="1206 [SMD]"]
  U1 = PCF8574 [package="DIP16 [THT]"]

nets:
  N1: IN12A1.pin2, MSPA52.C
  N2: IN12A1.pin3, MSPA51.C
  N3: IN12A1.pin4, MSPA50.C
  N4: IN12A1.pin5, MSPA49.C
  N5: IN12A1.pin6, MSPA48.C
  N6: IN12A1.pin7, MSPA43.C
  N7: IN12A1.pin8, MSPA42.C
  N8: IN12A1.pin9, MSPA44.C
  N9: IN12A1.pin0, MSPA45.C
  N10: IN12A1.pinAnode, MSPA46.C
  N11: IN12A1.pinNC, MSPA47.C
  N12: MSPA42.E, MSPA43.E, MSPA44.E, MSPA45.E, MSPA46.E, MSPA47.E, MSPA48.E, MSPA49.E, MSPA50.E, MSPA51.E, MSPA52.E
  N13: MSPA42.B, R10.Pin_0
  N14: MSPA43.B, R11.Pin_0
  N15: MSPA44.B, R9.Pin_0
  N16: MSPA45.B, R8.Pin_0
  N17: MSPA46.B, R7.Pin_0
  N18: MSPA47.B, R6.Pin_0
  N19: MSPA48.B, R5.Pin_0
  N20: MSPA49.B, R4.Pin_0
  N21: MSPA50.B, R3.Pin_0
  N22: MSPA51.B, R2.Pin_0
  N23: MSPA52.B, R1.Pin_0
  N24: R1.Pin_1, U1.P0
  N25: R2.Pin_1, U1.P1
  N26: R3.Pin_1, U1.P2
  N27: R4.Pin_1, U1.P3

custom parts:
  IN12A: A 12pin IN12A Nixie Tube
